// Logisim project PLU_V4.circ as structural Verilog: 16 circuits, main circuit main
module main (
);

  wire clock_1_out;
  wire [5:0] counter_1_q, counter_1_q_2;
  wire [7:0] rgb2hsv_1_v, slider_1_out;
  wire [15:0] rgb2hsv_1_s;
  wire [23:0] hsv2rgb_1_rgb_out, rom_1_data;
  wire [31:0] bit_extender_1_out, multiplier_1_out, rgb2hsv_1_h, subtractor_1_out, undriven;

  Clock clock_1 (.out(clock_1_out));
  Counter #(.max('hfff), .width(12)) counter_1 (
    .clk(clock_1_out), .Q({counter_1_q_2, counter_1_q}));  // open: clr, load, up, count, D, carry
  ROM #(.addrWidth(12), .dataWidth(24)) rom_1 (.addr({counter_1_q_2, counter_1_q}), .data(rom_1_data));
  // Probe on rom_1_data[23:16]
  // Probe on rom_1_data[15:8]
  Slider slider_1 (.out(slider_1_out));
  // Probe on rom_1_data[7:0]
  assign bit_extender_1_out = {{24{slider_1_out[7]}}, slider_1_out};  // Bit_Extender bit_extender_1
  Multiplier #(.width(32)) multiplier_1 (
    .a(bit_extender_1_out), .b(32'hff), .out(multiplier_1_out));  // open: cin, cout
  // Probe on multiplier_1_out
  // Probe on rgb2hsv_1_h
  RGB2HSV rgb2hsv_1 (
    .R_IN(rom_1_data[23:16]), .B_IN(rom_1_data[15:8]), .G_IN(rom_1_data[7:0]), .H(rgb2hsv_1_h),
    .S(rgb2hsv_1_s), .V(rgb2hsv_1_v));
  Subtractor #(.width(32)) subtractor_1 (
    .a(undriven), .b(multiplier_1_out), .out(subtractor_1_out));  // open: bin, bout
  // Probe on rgb2hsv_1_s
  // Probe on rgb2hsv_1_v
  // Probe on subtractor_1_out
  HSV2RGB hsv2rgb_1 (.H_IN(rgb2hsv_1_h), .S_IN(rgb2hsv_1_s), .V_IN(rgb2hsv_1_v), .RGB_OUT(hsv2rgb_1_rgb_out));
  // Probe on hsv2rgb_1_rgb_out[7:0]
  // Probe on hsv2rgb_1_rgb_out[15:8]
  // Probe on hsv2rgb_1_rgb_out[23:16]
  // RGB_Video #(.cursor("No Cursor"), .height(64), .scale(4), .width(64)) rgb_video_1: pin names not known; wires that end beside it: 1'b0, clock_1_out, 1'b1, counter_1_q, counter_1_q_2, {hsv2rgb_1_rgb_out[7:0], hsv2rgb_1_rgb_out[15:8], hsv2rgb_1_rgb_out[23:16]}

  // Notes on the sheet:
  //   contents of rom_1 (hex, n*v repeats v):
  //   131410 171710 1a1911 15170f e0e05 11272a 2a3137 480f08 4a1311 432f14 6f6016 816814 744a18 452f22
  //   9a6604 f8c940 f1d461 f7ca6f fba17d e25743 fa909a ff99ab fd3c4a 791008 4f201b 6d1e15 e85c64 debfd3
  //   adb39f b1a548 a36c71 b80324 c04929 dfad12 78a29d 5ba3cd 6fa5c1 4a98b4 6ba3a2 71a1c1 e2a078 89a094
  //   1e97c6 3c99b5 3798b4 3598b4 3197b4 2e96b2 2c95b2 2c94b1 2b94b1 2492af 2091ae 1d8fad 1b8eac 188cab
  //   108aa8 f88a7 c86a5 984a3 782a1 57f9f 47c9c 2799a 141611 1b1b13 1a1a12 12160f 131f1b 181d14 722826
  //   530e0e 43100e 3c2b12 545017 725412 6a3e1a 423536 754801 f4be31 f0ca4e faca75 fb9c7d de2e20 fb6274
  //   f6748c e85b48 622818 1a230c 310c00 ef8ea0 ffbfd1 c1673c 7d6c47 5d9dc4 b36797 cc8593 999148 4c98a7
  //   2387b1 cec2b4 a6d4dd 5c94b6 d2b598 8ca69b 939c8d 2d9ac5 3a99b5 3a99b5 3898b4 3497b4 3097b3 2e95b3
  //   2c94b1 2994b1 2692b0 2292ae 1f90ad 1c8eac 178cab 138aa9 1188a7 d86a5 a84a3 882a2 680a0 57d9d 27a9b
  //   1b1c15 1d1f16 191c13 161910 c1a12 5a272a 671818 2f0e0b 37120f 2d2611 3d3f17 4f3d16 552310 240d08
  //   6c4407 ebae2d f1c250 f9bd60 fa8456 d20702 ee2130 d64955 594623 745724 805b2e 7d320f fd2138 e76f9e
  //   ae6864 5c3c39 5a6660 e0b17b c9a292 55687f 399fd3 92b5ca d8bb98 f2b298 d8b2af b99d6d 3b8eb4 4ba3c4
  //   419bb3 3a9ab6 3a99b5 3899b5 3698b4 3097b3 2f96b3 2e96b2 2894b1 2793b0 2692b0 2291af 1d8fad 188dab
  //   178caa 128aa8 e87a6 b85a4 983a3 881a0 57e9e 37c9c 1f2015 222316 1e2014 12190f 241b16 672425 321410
  //   22130e 241810 202212 2c3017 312b14 4f2314 362625 63410e dc9629 f0b852 feaf5b f85e33 cf0100 e8222f
  //   eb626a 530d12 702700 ad965b d195ba bc0811 a90b15 b62c32 b5585a 6f473b c88063 dcd1cb 6d7c74 688db0
  //   95a4bb 9b7e58 cd847f 997f74 a19f82 3b7888 35a5cc 429bb7 3d9ab6 3a9ab6 3a9ab6 3799b5 3197b4 3197b4
  //   2f96b3 2b95b2 2894b1 2692b0 2592af 1f90ad 198eac 178cab 138ba9 1189a8 c87a5 a85a4 983a2 47f9f 37d9d
  //   1f2115 212216 1e2114 161a10 351913 39130e 2c120e 291811 1e1e13 1e2415 242a17 312b18 4b291b 312c28
  //   5a3613 c36b22 e7943b ea7a32 ec3e21 bf0a07 aa0205 f34861 d56d5d 753f0a 7b5614 ac7d87 9a162b 9e0000
  //   bb0d0c d43544 89141a 9d3e3e ddd1d7 ece1cc d8c4bb 496865 6a5d50 59a7d7 4c6258 815524 508a99 3ca5ca
  //   449cb8 409cb7 3c9ab7 3a9ab6 379ab6 3399b5 3398b4 3197b3 2b96b2 2795b2 2593b1 2493b0 1f91ae 1b8fad
  //   178dab 158caa 128aa8 e88a7 b86a5 983a3 681a1 47f9f 202216 202216 1a1e13 191a11 3c1812 4c1511 36130f
  //   241910 1f2315 212717 252c19 2c2e1b 312615 271304 87341c cf572c d16b2c cd561e d53513 ac0c0b 810000
  //   e84464 ffbeb2 c5542c 64000d 6f120e 940d13 ab090f c12029 d52536 d62934 ea97b3 667072 677942 a0856a
  //   dbb08d e8a7af 4b99c2 44a1c4 6a7873 67a1b2 399dbe 429cb8 409cb8 3e9cb7 3a9ab6 379ab6 3699b5 3398b5
  //   3197b4 2e97b3 2b95b2 2795b1 2593b0 2192af 1e90ae 198fad 158dab 148baa 1089a8 c87a6 a85a4 882a2 57fa0
  //   202216 1d2015 171c12 16180f 301711 451512 31140f 1c1b10 222617 252b19 232e1a 222b19 282d18 74533a
  //   e18b73 e88560 c55f24 c64d12 df3916 c10f0e 960000 cb222d ff6c82 dd242d a10c0f 690c09 850a0c ab0d13
  //   c92832 e54459 e43b53 ec5877 bb7c7c 487c83 799690 ea7365 ff4362 8e9db2 41a6c5 46afda 449ebd 489cb6
  //   439db8 409cb8 3e9cb8 3b9bb7 389ab6 3799b6 3599b5 3298b4 2f97b3 2d96b3 2995b2 2594b1 2293b0 1f91af
  //   1d8fad 188eab 138baa 108aa9 d88a7 a86a5 883a3 681a1 1d2014 1a1d12 161a11 10160e 1f170e 3a1911 2e1811
  //   1f2112 292d18 2a321b 1b2b18 1e2c18 856b49 e5b996 f1d4c3 f1c3aa cc7335 bc4000 f0471c dc2417 b90209
  //   b70000 ce151a c22128 aa0f15 950d11 940c0f ab0d13 cc2a35 ee5167 e8435c ea1d36 ff83a2 dfd9ff aeaa90
  //   d56e4a fa2236 9e8fa0 37a9c8 4a9fb9 489eb9 469eb9 439db9 419db8 3e9cb8 3c9cb8 3b9bb7 389ab6 3499b5
  //   3299b5 3098b4 2d97b4 2995b3 2794b2 2394b1 1f92af 1d90ae 198fad 128dab 108ba9 d89a8 b87a6 985a4 582a2
  //   191c12 1a1b12 151710 d150e 201d0f 3b1e11 2d1c12 222613 2f3319 2f371c 112513 3c4429 d5ab88 fad9c5
  //   ebd9cd f0d1bf d29356 b14b00 e85117 e4341b c70b0d cc070d c00810 ba1922 b3151b ab0d13 a60b0f b61219
  //   ca2832 e7485c f2516a f34b6d fc486f ff9db9 bba5ab b25452 f24f62 66a7c1 39a4c0 4da0bb 499fba 469eba
  //   459eb9 429db9 419db9 3f9db8 3d9cb8 3b9bb7 379ab6 3499b5 3399b5 2f98b4 2a97b3 2996b3 2494b1 2093b0
  //   1d91ae 1a90ae 158eac 118caa f8aa9 c88a7 986a5 783a3 171a11 191a11 16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
endmodule

module RGB2HSV (
  input  [7:0] R_IN,
  input  [7:0] B_IN,
  input  [7:0] G_IN,
  output [31:0] H,
  output [15:0] S,
  output [7:0] V
);

  wire [7:0] rgb_max_sel_1_diff, rgb_max_sel_1_idx, rgb_max_sel_1_max, rgb_max_sel_1_mid, rgb_max_sel_1_min;

  RGB_MAX_SEL rgb_max_sel_1 (
    .R_IN(R_IN), .G_IN(B_IN), .B_IN(G_IN), .MAX(rgb_max_sel_1_max), .IDX(rgb_max_sel_1_idx),
    .DIFF(rgb_max_sel_1_diff), .MID(rgb_max_sel_1_mid), .MIN(rgb_max_sel_1_min));
  H_CALC h_calc_1 (
    .MIN(rgb_max_sel_1_min), .IDX(rgb_max_sel_1_idx), .DIFF(rgb_max_sel_1_diff), .MID(rgb_max_sel_1_mid),
    .H(H));
  S_CALC s_calc_1 (.DIFF(rgb_max_sel_1_diff), .V(V), .S(S));
  V_CALC v_calc_1 (.MAX(rgb_max_sel_1_max), .V(V));
  // Probe on H
  // Probe on S
  // Probe on V
endmodule

module RGB_MAX_SEL (
  input  [7:0] R_IN,
  input  [7:0] G_IN,
  input  [7:0] B_IN,
  output [7:0] MAX,
  output [7:0] IDX,
  output [7:0] DIFF,
  output [7:0] MID,
  output [7:0] MIN
);

  wire comparator_1_eq, comparator_1_gt, comparator_1_lt, comparator_2_eq, comparator_2_gt, comparator_2_lt,
       comparator_3_eq, comparator_3_gt, comparator_3_lt, minmax_1_bmax, minmax_1_bmin, minmax_1_gmax,
       minmax_1_gmin, minmax_1_rmax, minmax_1_rmin, nor_1_out, or_1_out, or_2_out, or_3_out, or_4_out,
       or_5_out, or_6_out, rgbl_sel_1_bmin_1, rgbl_sel_1_bmin_2, rgbl_sel_1_gmin, rgbl_sel_1_rmin_1,
       rgbl_sel_1_rmin_2, rgbm_sel_1_bmax_1, rgbm_sel_1_bmax_2, rgbm_sel_1_gmax_1, rgbm_sel_1_gmax_2,
       rgbm_sel_1_rmax;
  wire [1:0] priority_encoder_1_out, priority_encoder_2_out;

  Comparator #(.mode("unsigned")) comparator_1 (
    .a(R_IN), .b(G_IN), .gt(comparator_1_gt), .eq(comparator_1_eq), .lt(comparator_1_lt));
  Comparator #(.mode("unsigned")) comparator_2 (
    .a(R_IN), .b(B_IN), .gt(comparator_2_gt), .eq(comparator_2_eq), .lt(comparator_2_lt));
  Comparator #(.mode("unsigned")) comparator_3 (
    .a(G_IN), .b(B_IN), .gt(comparator_3_gt), .eq(comparator_3_eq), .lt(comparator_3_lt));
  nor nor_1 (nor_1_out, comparator_1_eq, comparator_2_eq, comparator_3_eq);
  RGBM_SEL rgbm_sel_1 (
    .RG_G(comparator_1_gt), .GB_E(comparator_3_eq), .RG_L(comparator_1_lt), .RB_E(comparator_2_eq),
    .RB_G(comparator_2_gt), .RG_E(comparator_1_eq), .RB_L(comparator_2_lt), .RMAX(rgbm_sel_1_rmax),
    .GMAX_1(rgbm_sel_1_gmax_1), .GMAX_2(rgbm_sel_1_gmax_2), .BMAX_1(rgbm_sel_1_bmax_1),
    .BMAX_2(rgbm_sel_1_bmax_2));
  MinMax minmax_1 (
    .RG_G(comparator_1_gt), .RG_L(comparator_1_lt), .RB_G(comparator_2_gt), .RB_L(comparator_2_lt),
    .GB_G(comparator_3_gt), .GB_L(comparator_3_lt), .EN(nor_1_out), .RMAX(minmax_1_rmax),
    .GMAX(minmax_1_gmax), .BMAX(minmax_1_bmax), .RMIN(minmax_1_rmin), .GMIN(minmax_1_gmin),
    .BMIN(minmax_1_bmin));
  RGBL_SEL rgbl_sel_1 (
    .RG_G(comparator_1_gt), .GB_E(comparator_3_eq), .RG_L(comparator_1_lt), .RB_E(comparator_2_eq),
    .RB_L(comparator_2_lt), .RG_E(comparator_1_eq), .RB_G(comparator_2_gt), .RMIN_1(rgbl_sel_1_rmin_1),
    .RMIN_2(rgbl_sel_1_rmin_2), .BMIN_1(rgbl_sel_1_bmin_1), .GMIN(rgbl_sel_1_gmin), .BMIN_2(rgbl_sel_1_bmin_2));
  or or_1 (or_1_out, minmax_1_rmax, rgbm_sel_1_rmax);
  or or_2 (or_2_out, rgbl_sel_1_rmin_2, minmax_1_bmin, rgbl_sel_1_bmin_2, rgbl_sel_1_bmin_1);
  or or_3 (or_3_out, minmax_1_gmax, rgbm_sel_1_gmax_1, rgbm_sel_1_gmax_2);
  or or_4 (or_4_out, minmax_1_bmax, rgbm_sel_1_bmax_1, rgbm_sel_1_bmax_2);
  or or_5 (or_5_out, minmax_1_gmin, rgbl_sel_1_gmin);
  or or_6 (or_6_out, minmax_1_rmin, rgbl_sel_1_rmin_2, rgbl_sel_1_rmin_1);
  RGB_SEL rgb_sel_1 (
    .R_IN(R_IN), .G_IN(G_IN), .B_IN(B_IN), .R_EN(or_1_out), .G_EN(or_3_out), .B_EN(or_4_out), .RGB_OUT(MAX));
  // Probe on priority_encoder_1_out
  Priority_Encoder #(.select(2)) priority_encoder_1 (
    .in0(or_1_out), .in1(or_3_out), .in2(or_4_out), .out(priority_encoder_1_out));  // open: in3, gs, en_out, en_in
  // Probe on priority_encoder_2_out
  Priority_Encoder #(.select(2)) priority_encoder_2 (
    .in0(or_6_out), .in1(or_5_out), .in2(or_2_out), .out(priority_encoder_2_out));  // open: in3, gs, en_out, en_in
  RGB_SEL rgb_sel_2 (
    .R_IN(R_IN), .G_IN(G_IN), .B_IN(B_IN), .R_EN(or_6_out), .G_EN(or_5_out), .B_EN(or_2_out), .RGB_OUT(MIN));
  Subtractor subtractor_1 (.a(MAX), .b(MIN), .out(DIFF));  // open: bin, bout
  // Probe on MAX
  Multiplexer #(.select(4), .width(8)) multiplexer_1 (
    .in0({8{1'b1}}), .in1(8'h2), .in2(8'h3), .in3({8{1'b1}}), .in4(8'h5), .in5({8{1'b1}}), .in6(8'h4),
    .in7({8{1'b1}}), .in8({8{1'b0}}), .in9(8'h1), .in10({8{1'b1}}), .in11({8{1'b1}}), .in12({8{1'b1}}),
    .in13({8{1'b1}}), .in14({8{1'b1}}), .in15({8{1'b1}}), .out(IDX),
    .sel({priority_encoder_2_out, priority_encoder_1_out}));
  // Probe on DIFF
  // Probe on MIN
  RGB_MID_SEL rgb_mid_sel_1 (
    .RMAX(or_1_out), .RMIN(or_6_out), .GMAX(or_3_out), .GMIN(or_5_out), .BMAX(or_4_out), .BMIN(or_2_out),
    .R(B_IN), .G(G_IN), .B(R_IN), .MID(MID));
  // Probe on MID

  // Notes on the sheet:
  //   RG
  //   RB
  //   GB
endmodule

module H_CALC (
  input  [7:0] MIN,
  input  [7:0] IDX,
  input  [7:0] DIFF,
  input  [7:0] MID,
  output [31:0] H
);

  wire bit_extender_3_out;
  wire [7:0] and_1_out, subtractor_1_out;
  wire [31:0] adder_1_out, bit_extender_1_out, bit_extender_2_out, bit_extender_4_out, divider_1_out,
       multiplexer_1_out, multiplier_1_out, shifter_1_out, subtractor_2_out;

  // Probe on MIN
  // Probe on DIFF
  // Probe on MID
  // Probe on subtractor_1_out
  Subtractor subtractor_1 (.a(MID), .b(MIN), .out(subtractor_1_out));  // open: bin, bout
  // Probe on bit_extender_1_out
  assign bit_extender_1_out = {{24{1'b0}}, subtractor_1_out};  // Bit_Extender bit_extender_1
  assign bit_extender_2_out = {{24{1'b0}}, DIFF};  // Bit_Extender bit_extender_2
  assign and_1_out = IDX & 8'h1;  // AND_Gate and_1, 8 bits wide
  // Probe on shifter_1_out
  Shifter #(.width(32)) shifter_1 (.in(bit_extender_1_out), .\dist (5'b10000), .out(shifter_1_out));
  // Probe on and_1_out
  Bit_Extender #(.out_width(1), .\type ("input")) bit_extender_3 (
    .in(and_1_out), .out(bit_extender_3_out));  // open: extend
  // Probe on divider_1_out
  Divider #(.width(32)) divider_1 (.a(shifter_1_out), .b(bit_extender_2_out), .out(divider_1_out));  // open: upper, rem
  // Probe on adder_1_out
  Adder #(.width(32)) adder_1 (.a(divider_1_out), .b(32'h1), .out(adder_1_out));  // open: cin, cout
  Subtractor #(.width(32)) subtractor_2 (.a(32'hffff), .b(adder_1_out), .out(subtractor_2_out));  // open: bin, bout
  Multiplexer #(.width(32)) multiplexer_1 (
    .in0(adder_1_out), .in1(subtractor_2_out), .out(multiplexer_1_out), .sel(bit_extender_3_out));
  // Probe on multiplexer_1_out
  // Probe on 32'hffff
  assign bit_extender_4_out = {{24{1'b0}}, IDX};  // Bit_Extender bit_extender_4
  // Probe on IDX
  Multiplier #(.width(32)) multiplier_1 (
    .a(32'hffff), .b(bit_extender_4_out), .out(multiplier_1_out));  // open: cin, cout
  Adder #(.width(32)) adder_2 (.a(multiplexer_1_out), .b(multiplier_1_out), .out(H));  // open: cin, cout
  // Probe on multiplier_1_out
  // Probe on H

  // Notes on the sheet:
  //   E
  //   F
endmodule

module S_CALC (
  input  [7:0] DIFF,
  input  [7:0] V,
  output [15:0] S
);

  wire [23:0] bit_extender_1_out, bit_extender_2_out, divider_1_out, shifter_1_out, subtractor_1_out;

  // Probe on DIFF
  assign bit_extender_1_out = {{16{1'b0}}, DIFF};  // Bit_Extender bit_extender_1
  // Probe on V
  assign bit_extender_2_out = {{16{1'b0}}, V};  // Bit_Extender bit_extender_2
  // Probe on 5'b10000
  // Probe on bit_extender_1_out
  // Probe on shifter_1_out
  Shifter #(.width(24)) shifter_1 (.in(bit_extender_1_out), .\dist (5'b10000), .out(shifter_1_out));
  Subtractor #(.width(24)) subtractor_1 (.a(shifter_1_out), .b(24'h1), .out(subtractor_1_out));  // open: bin, bout
  // Probe on bit_extender_2_out
  // Probe on divider_1_out
  Divider #(.width(24)) divider_1 (
    .a(subtractor_1_out), .b(bit_extender_2_out), .out(divider_1_out));  // open: upper, rem
  Bit_Extender #(.in_width(24), .\type ("zero")) bit_extender_3 (.in(divider_1_out), .out(S));
endmodule

module V_CALC (
  input  [7:0] MAX,
  output [7:0] V
);


  assign V = MAX;
endmodule

module MinMax (
  input  RG_G,
  input  RG_L,
  input  RB_G,
  input  RB_L,
  input  GB_G,
  input  GB_L,
  input  EN,
  output RMAX,
  output GMAX,
  output BMAX,
  output RMIN,
  output GMIN,
  output BMIN
);

  wire and_1_out, and_2_out, and_3_out, and_4_out, and_5_out, and_6_out;

  and and_1 (and_1_out, RG_G, RB_G);
  and and_2 (and_2_out, RG_L, GB_G);
  and and_3 (and_3_out, RB_L, GB_L);
  and and_4 (and_4_out, RG_L, RB_L);
  and and_5 (and_5_out, RG_G, GB_L);
  and and_6 (and_6_out, RB_G, GB_G);
  and and_7 (RMAX, and_1_out, EN);
  and and_8 (GMAX, and_2_out, EN);
  and and_9 (BMAX, and_3_out, EN);
  and and_10 (RMIN, and_4_out, EN);
  and and_11 (GMIN, and_5_out, EN);
  and and_12 (BMIN, and_6_out, EN);

  // Notes on the sheet:
  //   R max
  //   G max
  //   B max
  //   R min
  //   G min
  //   B min
endmodule

module RGB_SEL (
  input  [7:0] R_IN,
  input  [7:0] G_IN,
  input  [7:0] B_IN,
  input  R_EN,
  input  G_EN,
  input  B_EN,
  output [7:0] RGB_OUT
);

  wire [1:0] priority_encoder_1_out;
  wire [7:0] and_1_out, and_2_out, and_3_out, bit_extender_1_out, bit_extender_2_out, bit_extender_3_out;

  assign bit_extender_1_out = {{7{1'b1}}, R_EN};  // Bit_Extender bit_extender_1
  assign bit_extender_2_out = {{7{1'b1}}, G_EN};  // Bit_Extender bit_extender_2
  assign bit_extender_3_out = {{7{1'b1}}, B_EN};  // Bit_Extender bit_extender_3
  assign and_1_out = bit_extender_1_out & R_IN;  // AND_Gate and_1, 8 bits wide
  assign and_2_out = bit_extender_2_out & G_IN;  // AND_Gate and_2, 8 bits wide
  assign and_3_out = bit_extender_3_out & B_IN;  // AND_Gate and_3, 8 bits wide
  // Probe on and_1_out
  Priority_Encoder #(.select(2)) priority_encoder_1 (
    .in0(R_EN), .in1(G_EN), .in2(B_EN), .in3(1'b0), .out(priority_encoder_1_out));  // open: gs, en_out, en_in
  // Probe on RGB_OUT
  Multiplexer #(.select(2), .width(8)) multiplexer_1 (
    .in0(and_1_out), .in1(and_2_out), .in2(and_3_out), .in3({8{1'b0}}), .out(RGB_OUT),
    .sel(priority_encoder_1_out));
endmodule

module RGBM_SEL (
  input  RG_G,
  input  GB_E,
  input  RG_L,
  input  RB_E,
  input  RB_G,
  input  RG_E,
  input  RB_L,
  output RMAX,
  output GMAX_1,
  output GMAX_2,
  output BMAX_1,
  output BMAX_2
);

  wire and_1_out, and_2_out, and_3_out, and_5_out;

  and and_1 (and_1_out, GB_E, RB_E, RG_E);
  and and_2 (and_2_out, RG_G, GB_E);
  and and_3 (and_3_out, GB_E, RG_L);
  and and_4 (BMAX_1, RG_G, RB_E);
  and and_5 (and_5_out, RB_E, RG_L);
  and and_6 (GMAX_2, RB_G, RG_E);
  and and_7 (BMAX_2, RG_E, RB_L);
  or or_1 (RMAX, and_1_out, and_2_out);
  or or_2 (GMAX_1, and_3_out, and_5_out);
endmodule

module RGBL_SEL (
  input  RG_G,
  input  GB_E,
  input  RG_L,
  input  RB_E,
  input  RB_L,
  input  RG_E,
  input  RB_G,
  output RMIN_1,
  output RMIN_2,
  output BMIN_1,
  output GMIN,
  output BMIN_2
);

  wire and_2_out, and_4_out, and_6_out, and_7_out;

  and and_1 (BMIN_1, RG_G, GB_E);
  and and_2 (and_2_out, GB_E, RG_L);
  and and_3 (GMIN, RG_G, RB_E);
  and and_4 (and_4_out, RB_E, RG_L);
  and and_5 (RMIN_1, RB_L, RG_E);
  and and_6 (and_6_out, RG_E, RB_G);
  and and_7 (and_7_out, RG_E, RB_E, GB_E);
  or or_1 (BMIN_2, and_6_out, and_7_out);
  or or_2 (RMIN_2, and_2_out, and_4_out);
endmodule

module HSV2RGB (
  input  [31:0] H_IN,
  input  [15:0] S_IN,
  input  [7:0] V_IN,
  output [23:0] RGB_OUT
);

  wire [7:0] c_calc_1_c, dmcalc_1_m, ifcalc_1_i;
  wire [15:0] dmcalc_1_d;
  wire [31:0] ifcalc_1_f;

  // Probe on H_IN
  // Probe on V_IN
  // Probe on S_IN
  IFCALC ifcalc_1 (.H(H_IN), .I(ifcalc_1_i), .F(ifcalc_1_f));
  DMCALC dmcalc_1 (.S(S_IN), .V(V_IN), .D(dmcalc_1_d), .M(dmcalc_1_m));
  // Probe on ifcalc_1_i
  // Probe on ifcalc_1_f
  // Probe on dmcalc_1_m
  // Probe on dmcalc_1_d
  C_CALC c_calc_1 (.F(ifcalc_1_f), .D(dmcalc_1_d), .M(dmcalc_1_m), .c(c_calc_1_c));
  // Probe on c_calc_1_c
  RGB_ORDER_DECODER rgb_order_decoder_1 (.C(c_calc_1_c), .M(dmcalc_1_m), .V(V_IN), .I(ifcalc_1_i), .RGB_OUT(RGB_OUT));
endmodule

module DMCALC (
  input  [15:0] S,
  input  [7:0] V,
  output [15:0] D,
  output [7:0] M
);

  wire [31:0] adder_1_out, bit_extender_1_out, bit_extender_2_out, multiplier_1_out, shifter_1_out,
       subtractor_1_out;

  // Probe on S
  // Probe on V
  assign bit_extender_1_out = {{16{1'b0}}, S};  // Bit_Extender bit_extender_1
  assign bit_extender_2_out = {{24{1'b0}}, V};  // Bit_Extender bit_extender_2
  // Probe on multiplier_1_out
  Multiplier #(.width(32)) multiplier_1 (
    .a(bit_extender_1_out), .b(bit_extender_2_out), .out(multiplier_1_out));  // open: cin, cout
  Shifter #(.shift("lr"), .width(32)) shifter_1 (.in(multiplier_1_out), .\dist (5'b10000), .out(shifter_1_out));
  // Probe on 5'b10000
  // Probe on shifter_1_out
  Adder #(.width(32)) adder_1 (.a(shifter_1_out), .b(32'h1), .out(adder_1_out));  // open: cin, cout
  // Probe on 32'h1
  // Probe on adder_1_out
  Subtractor #(.width(32)) subtractor_1 (
    .a(bit_extender_2_out), .b(adder_1_out), .out(subtractor_1_out));  // open: bin, bout
  Bit_Extender #(.in_width(32), .\type ("zero")) bit_extender_3 (.in(adder_1_out), .out(D));
  Bit_Extender #(.in_width(32), .out_width(8), .\type ("zero")) bit_extender_4 (.in(subtractor_1_out), .out(M));
  // Probe on subtractor_1_out

  // Notes on the sheet:
  //   D
endmodule

module IFCALC (
  input  [31:0] H,
  output [7:0] I,
  output [31:0] F
);

  wire and_1_out, and_2_out, and_3_out, and_4_out, comparator_1_eq, comparator_1_gt, comparator_1_lt,
       comparator_2_eq, comparator_2_gt, comparator_2_lt, comparator_3_eq, comparator_3_gt, comparator_3_lt,
       comparator_4_eq, comparator_4_gt, comparator_4_lt, comparator_5_eq, comparator_5_gt, comparator_5_lt,
       or_1_out, or_2_out, or_3_out, or_4_out, or_5_out, or_6_out;
  wire [2:0] priority_encoder_1_out;
  wire [31:0] adder_1_out, bit_extender_1_out, bit_extender_2_out, multiplexer_2_out, multiplier_1_out,
       multiplier_2_out, multiplier_3_out, multiplier_4_out, multiplier_5_out, subtractor_1_out,
       subtractor_2_out;

  assign bit_extender_1_out = {{16{1'b0}}, {16{1'b1}}};  // Bit_Extender bit_extender_1
  // Probe on bit_extender_1_out
  // Probe on H
  Multiplier #(.width(32)) multiplier_1 (.a(bit_extender_1_out), .b(32'h2), .out(multiplier_1_out));  // open: cin, cout
  Multiplier #(.width(32)) multiplier_2 (.a(bit_extender_1_out), .b(32'h3), .out(multiplier_2_out));  // open: cin, cout
  Multiplier #(.width(32)) multiplier_3 (.a(bit_extender_1_out), .b(32'h4), .out(multiplier_3_out));  // open: cin, cout
  Multiplier #(.width(32)) multiplier_4 (.a(bit_extender_1_out), .b(32'h5), .out(multiplier_4_out));  // open: cin, cout
  Comparator #(.mode("unsigned"), .width(32)) comparator_1 (
    .a(H), .b(bit_extender_1_out), .gt(comparator_1_gt), .eq(comparator_1_eq), .lt(comparator_1_lt));
  Comparator #(.mode("unsigned"), .width(32)) comparator_2 (
    .a(H), .b(multiplier_1_out), .gt(comparator_2_gt), .eq(comparator_2_eq), .lt(comparator_2_lt));
  Comparator #(.mode("unsigned"), .width(32)) comparator_3 (
    .a(H), .b(multiplier_2_out), .gt(comparator_3_gt), .eq(comparator_3_eq), .lt(comparator_3_lt));
  Comparator #(.mode("unsigned"), .width(32)) comparator_4 (
    .a(H), .b(multiplier_3_out), .gt(comparator_4_gt), .eq(comparator_4_eq), .lt(comparator_4_lt));
  Comparator #(.mode("unsigned"), .width(32)) comparator_5 (
    .a(H), .b(multiplier_4_out), .gt(comparator_5_gt), .eq(comparator_5_eq), .lt(comparator_5_lt));
  or or_1 (or_1_out, comparator_1_gt, comparator_1_eq);
  or or_2 (or_2_out, comparator_2_gt, comparator_2_eq);
  or or_3 (or_3_out, comparator_3_gt, comparator_3_eq);
  or or_4 (or_4_out, comparator_4_gt, comparator_4_eq);
  or or_5 (or_5_out, comparator_5_gt, comparator_5_eq);
  and and_1 (and_1_out, or_1_out, comparator_2_lt);
  and and_2 (and_2_out, or_2_out, comparator_3_lt);
  and and_3 (and_3_out, or_3_out, comparator_4_lt);
  and and_4 (and_4_out, or_4_out, comparator_5_lt);
  Priority_Encoder priority_encoder_1 (
    .in0(comparator_1_lt), .in1(and_1_out), .in2(and_2_out), .in3(and_3_out), .in4(and_4_out),
    .in5(or_5_out), .in6(1'b0), .in7(1'b0), .out(priority_encoder_1_out));  // open: en_in, gs, en_out
  Multiplexer #(.select(3), .width(8)) multiplexer_1 (
    .in0({8{1'b0}}), .in1(8'h1), .in2(8'h2), .in3(8'h3), .in4(8'h4), .in5(8'h5), .in6(8'h6), .in7({8{1'b0}}),
    .out(I), .sel(priority_encoder_1_out));
  assign bit_extender_2_out = {{24{1'b0}}, I};  // Bit_Extender bit_extender_2
  Multiplier #(.width(32)) multiplier_5 (
    .a(bit_extender_2_out), .b(bit_extender_1_out), .out(multiplier_5_out));  // open: cin, cout
  // Probe on multiplier_5_out
  Subtractor #(.width(32)) subtractor_1 (.a(H), .b(multiplier_5_out), .out(subtractor_1_out));  // open: bin, bout
  // Probe on subtractor_1_out
  // Probe on adder_1_out
  Adder #(.width(32)) adder_1 (.a(subtractor_1_out), .b(32'h1), .out(adder_1_out));  // open: cin, cout
  // Probe on multiplexer_2_out
  Multiplexer #(.width(32)) multiplexer_2 (
    .in0(subtractor_1_out), .in1(adder_1_out), .out(multiplexer_2_out), .sel(comparator_1_lt));
  Subtractor #(.width(32)) subtractor_2 (
    .a(bit_extender_1_out), .b(multiplexer_2_out), .out(subtractor_2_out));  // open: bin, bout
  // Probe on bit_extender_1_out
  or or_6 (or_6_out, and_1_out, and_3_out, or_5_out);
  // Probe on subtractor_2_out
  Multiplexer #(.width(32)) multiplexer_3 (.in0(multiplexer_2_out), .in1(subtractor_2_out), .out(F), .sel(or_6_out));
  // Probe on F

  // Notes on the sheet:
  //   E
  //   I = 0
  //   I = 1
  //   I = 2
  //   I = 3
  //   I = 4
  //   I = 5
endmodule

module C_CALC (
  input  [31:0] F,
  input  [15:0] D,
  input  [7:0] M,
  output [7:0] c
);

  wire [7:0] bit_extender_2_out;
  wire [31:0] bit_extender_1_out, multiplier_1_out, shifter_1_out;

  // Probe on F
  assign bit_extender_1_out = {{16{1'b0}}, D};  // Bit_Extender bit_extender_1
  // Probe on bit_extender_1_out
  Multiplier #(.width(32)) multiplier_1 (.a(F), .b(bit_extender_1_out), .out(multiplier_1_out));  // open: cin, cout
  // Probe on multiplier_1_out
  // Probe on M
  // Probe on shifter_1_out
  Shifter #(.shift("lr"), .width(32)) shifter_1 (.in(multiplier_1_out), .\dist (5'b10000), .out(shifter_1_out));
  Bit_Extender #(.in_width(32), .out_width(8), .\type ("zero")) bit_extender_2 (
    .in(shifter_1_out), .out(bit_extender_2_out));
  Adder adder_1 (.a(bit_extender_2_out), .b(M), .out(c));  // open: cin, cout
  // Probe on c
endmodule

module RGB_ORDER_DECODER (
  input  [7:0] C,
  input  [7:0] M,
  input  [7:0] V,
  input  [7:0] I,
  output [23:0] RGB_OUT
);

  wire comparator_1_eq, comparator_2_eq, comparator_3_eq, comparator_4_eq, comparator_5_eq, comparator_6_eq;
  wire [2:0] priority_encoder_1_out;

  Comparator #(.mode("unsigned")) comparator_1 (.a(I), .b({8{1'b0}}), .eq(comparator_1_eq));  // open: gt, lt
  Comparator #(.mode("unsigned")) comparator_2 (.a(I), .b(8'h1), .eq(comparator_2_eq));  // open: gt, lt
  Comparator #(.mode("unsigned")) comparator_3 (.a(I), .b(8'h2), .eq(comparator_3_eq));  // open: gt, lt
  Comparator #(.mode("unsigned")) comparator_4 (.a(I), .b(8'h3), .eq(comparator_4_eq));  // open: gt, lt
  Comparator #(.mode("unsigned")) comparator_5 (.a(I), .b(8'h4), .eq(comparator_5_eq));  // open: gt, lt
  Comparator #(.mode("unsigned")) comparator_6 (.a(I), .b(8'h5), .eq(comparator_6_eq));  // open: gt, lt
  Priority_Encoder priority_encoder_1 (
    .in0(comparator_1_eq), .in1(comparator_2_eq), .in2(comparator_3_eq), .in3(comparator_4_eq),
    .in4(comparator_5_eq), .in5(comparator_6_eq), .in6(1'b0), .in7(1'b0), .out(priority_encoder_1_out));  // open: en_in, gs, en_out
  Multiplexer #(.select(3), .width(24)) multiplexer_1 (
    .in0({M, C, V}), .in1({M, V, C}), .in2({C, V, M}), .in3({V, C, M}), .in4({V, M, C}), .in5({C, M, V}),
    .in6({24{1'b0}}), .in7({24{1'b0}}), .out(RGB_OUT), .sel(priority_encoder_1_out));

  // Notes on the sheet:
  //   I = 0
  //   I = 2
  //   I = 3
  //   I = 4
  //   I = 5
  //   I = 1
endmodule

module RGB_MID_SEL (
  input  RMAX,
  input  RMIN,
  input  GMAX,
  input  GMIN,
  input  BMAX,
  input  BMIN,
  input  [7:0] R,
  input  [7:0] G,
  input  [7:0] B,
  output [7:0] MID
);

  wire and_1_out, and_2_out, and_3_out, or_1_out, or_2_out, or_3_out, or_4_out, or_5_out, or_6_out;
  wire [1:0] priority_encoder_1_out;

  or or_1 (or_1_out, RMAX, RMIN);
  or or_2 (or_2_out, GMAX, GMIN);
  or or_3 (or_3_out, RMAX, RMIN);
  or or_4 (or_4_out, BMAX, BMIN);
  or or_5 (or_5_out, GMAX, GMIN);
  or or_6 (or_6_out, BMAX, BMIN);
  and and_1 (and_1_out, or_1_out, or_2_out);
  and and_2 (and_2_out, or_3_out, or_4_out);
  and and_3 (and_3_out, or_5_out, or_6_out);
  Priority_Encoder #(.select(2)) priority_encoder_1 (
    .in0(and_1_out), .in1(and_2_out), .in2(and_3_out), .out(priority_encoder_1_out));  // open: in3, gs, en_out, en_in
  Multiplexer #(.select(2), .width(8)) multiplexer_1 (
    .in0(R), .in1(G), .in2(B), .out(MID), .sel(priority_encoder_1_out));  // open: in3

  // Notes on the sheet:
  //   mid = b
  //   mid = g
  //   mid = r
endmodule
