// Logisim project PLUV2.circ as structural Verilog: 5 circuits, main circuit main
module main (
);

  wire clock_1_out, d_ff_1_q, d_ff_1_qn, plu_1_pixel_clk;
  wire [1:0] rom_1_data_2;
  wire [3:0] counter_1_q;
  wire [11:0] counter_2_q;
  wire [23:0] plu_1_rgb_output_24, rom_2_data, rom_3_data;
  wire [29:0] rom_1_data;

  D_Flip_Flop d_ff_1 (.D(d_ff_1_qn), .clk(clock_1_out), .Q(d_ff_1_q), .Qn(d_ff_1_qn));  // open: preset, reset
  Counter #(.max('hf), .width(4)) counter_1 (
    .clr(rom_1_data_2[1]), .clk(d_ff_1_q), .D(4'b1111), .Q(counter_1_q));  // open: load, up, count, carry
  ROM #(.addrWidth(4), .dataWidth(32)) rom_1 (.addr(counter_1_q), .data({rom_1_data_2, rom_1_data}));
  ROM #(.addrWidth(12), .dataWidth(24)) rom_2 (.addr(counter_2_q), .data(rom_2_data));
  ROM #(.addrWidth(4), .dataWidth(24)) rom_3 (.addr(counter_1_q), .data(rom_3_data));
  Clock clock_1 (.out(clock_1_out));
  // Probe on rom_1_data[29:27]
  // Probe on rom_1_data[26:24]
  // Probe on rom_1_data[23:18]
  // Probe on rom_1_data[17:0]
  // Probe on rom_2_data
  Counter #(.max('hfff), .width(12)) counter_2 (
    .clk(plu_1_pixel_clk), .D({12{1'b1}}), .Q(counter_2_q));  // open: clr, load, up, count, carry
  PLU plu_1 (
    .DATA_A_IN_24(rom_2_data), .DATA_B_IN_24(rom_3_data), .EN_A_3(rom_1_data[29:27]),
    .EN_B_3(rom_1_data[26:24]), .Channel_Swap_6(rom_1_data[23:18]), .CLK(clock_1_out),
    .opcode_in_18(rom_1_data[17:0]), .RGB_OUTPUT_24(plu_1_rgb_output_24), .pixel_clk(plu_1_pixel_clk));
  // Probe on plu_1_rgb_output_24
  // RGB_Video #(.cursor("No Cursor"), .height(64), .scale(8), .width(64)) rgb_video_1: pin names not known; wires that end beside it: plu_1_pixel_clk, 1'b1, counter_2_q[5:0], counter_2_q[11:6], plu_1_rgb_output_24

  // Notes on the sheet:
  //   contents of rom_1 (hex, n*v repeats v):
  //   3f190410 14*3f180000 3f1b0c30
  //   contents of rom_2 (hex, n*v repeats v):
  //   6*ffffff 8*d c b b a a b 9 4 6 5 8 8 6 7 d 9 5 6 3 4*0 3 5 5*4 a b 4*a c 4 0 0 1 6 6*0 8*ffffff 8*d
  //   c b b a a b 9 4 6 5 8 8 6 7 d 9 5 5 5 3 4 0 b0c0f 151518 0 6 5 5 4 7 c 5*a c 4 0 0 1 6 6*0 8*ffffff
  //   8*d c b b a a b 9 4 6 5 8 8 5 0 0 3 6 5 5 4 4 0 626565 979c9b 0 3 5 5 4 8 c 5*a c 4 0 0 1 6 6*0
  //   8*ffffff 8*d c b b a a b 9 4 6 6 2 0 0 191920 292935 1 0 3 5 5 3 0 a8a9a6 ffffff 1b1b1f 4*0 9 c 5*a
  //   c 4 0 0 1 6 6*0 8*ffffff 8*d c b b a a b 9 5 2 0 0 47464d 9d9999 dbd7d3 faf9f0 c6c5c3 414148 0 0 2 0
  //   5 d7d7d2 ffffff 99999a 0 0 1 1 a c 5*a c 4 0 0 1 6 6*0 8*ffffff 8*e c d e b a a 8 0 90911 6f6c6e
  //   f1ece6 ffffff ffffff fbf7f1 eae2d7 fdfbf5 ffffff b7b5b4 7060d 0 0 20202b fefef8 ffffff ffffff 38373c
  //   0 5 6 d b a 4*b d 5 0 0 1 6 6*0 8*ffffff 7*c e 7 4 6 8 c e 4 2 6b6970 d6d2cd b4b2af a2a1a1 e6e2da
  //   ffffff fffffe eee5dc ddd6cf ffffff eeedec 2f2c2f 0 27262f fffffc fffff9 ffffff c0bfbf 0 0 5 0 2 b
  //   4*9 a 2 0 0 1 6 6*0 8*ffffff 7*4 3 7070c 30303 0 7 7 a 7 0 0 0 232631 565b63 60636a 8f8e91 dfd8d1
  //   ffffff fefaf1 dbd3cc ffffff f3f3f1 111013 30205 f7f5ed ffffff fcfcf2 ffffff 4d4a4d 0 2 0 1b1b21
  //   40410 7 9 9 b 6 4*0 1 6*0 8*ffffff 6*3 2 0 6a676b 5e5e61 0 2 3 0 0 8080d 5f6064 cdc9c6 fffff6 fff7ed
  //   d7cfca aeaaaa a6a1a1 cfc7c3 fffaf1 f4ede4 e1ddd6 ffffff dddddc 26262a c4c4bc ffffff f7f6ec ffffff
  //   9a9b9a 0 0 45494a 969a9b 0 6 9 9 a 2 0 0 0 50505 29282c 10104 0 1 1 1 2 8*ffffff 6*a 8 0 928d8b
  //   ffffff 5b5d63 0 0 2 52505a d7d6d2 ffffff fffffd f1ede5 ece7df f8f2ea fffff9 f9f4eb dcd5cf efeae2
  //   fffff6 e3ded8 eeede4 ffffff bcbec0 9a9b98 fbfbee f5f6eb fffff7 c2c7be 0 2d2f33 fbfffc a7a7a4 0 8 c d
  //   9 4*0 5a5a54 d4d0c6 0 6 b b a 8 8*ffffff 6*b 9 0 8b8c8b fffffc ffffff c5c6c0 9d9d9d dddcd9 ffffff
  //   fefefc f8f8ef fffff8 fffffe fffff9 fefef2 f4f4ea eae9e1 f1ebe3 fffbf7 fffbf3 efe9e0 e9e4df fffff6
  //   fdfdf7 c1c0bc dcddd3 f2f6eb fcfff5 a7aca5 494d51 f1fff3 f7fff1 7a7073 0 4 8 9 7 3 0 0 10104 fcfae7
  //   c4beb0 0 2 5 9 a 6 8*ffffff 6*4 3 0 4d5359 fcfff6 f7f9ea fffffb ffffff ffffff ffffff fffffd fffff8
  //   fffff7 fffff7 fffff5 fffff3 fffff5 fffffa fffffb aa9d9d cabfbd fffffe ebe4df f8f6ed fefff1 e9eadf
  //   e1e3d9 ebefe2 f6fcee bcc2bb d8e0da f9fffb dad6cd 5e5558 0 3 0 1 6 5 0 0 aba9a3 ffffff 766e66 0 0 4 a
  //   a 5 8*ffffff 6*a 9 0 2c2b31 b5b2af e4e5d9 fffff7 f4f6e9 fafbf2 fffff9 6*fffff7 fffff4 fffff3 ffffff
  //   465d63 7b8a8e ffffff ece5df f0efe7 fefff2 f6f9ec fffff7 f8fcf0 cdd4cd aeb5b1 b2bcb5 919290 6e6770
  //   11131c 5050c 20209 0 4 6 0 0 918d8a ffffff fffee3 363132 0 6 a b 9 4 8*ffffff 5*5 6 6 0 312e35
  //   d3cec7 b2b0ab cdccc7 eeefe7 9*fffff7 fffffc fff2e4 2a838d 2e8d95 ffe1d6 fafaf5 edeae2 ffffff f1f2ec
  //   b6bbb6 9fa29b a5a498 b9b7a7 cac8b2 bcb6a3 7e7d77 30333c 2d2e38 5*0 a29a91 ffffff fffff6 b4a89c 0 0 8
  //   9 a 9 4 8*ffffff 5*0 3 3 0 0 7b7d7e f6f6ea dcdcd2 f1f0e9 fcfbf4 fdfcf4 fffef6 fffff7 fffff7 fffff6
  //   fffff8 ffffff ffffff ffffff fffffb 597e88 a5bb 75a29d f3d8d3 fefefc d0d2cc a6a49c bab3a0 e0d3b7
  //   ffffdf ffffec ffffea fffff0 fffff9 fffee5 b9b19e 534f4f d0c15 0 221e24 ccc1b2 ffffff fffffe e9deca
  //   222126 0 0 0 c f e a 8*ffffff 7*0 3d3c43 7b7b7c 8e8f8f dbd9d0 f7f8ea fefff6 fffffc fffffe fffff8
  //   fffff6 fffff7 fffffb f7f6ef cbcfcc f1e6de dfcdc3 bec3b7 5d7779 abc3 cee2 447781 e5bdaf cfc8b3 f2ebcf
  //   ffffea fffdde fff2d5 fff2d6 fff5db fff4da fff3d6 fffddf fffffa fffffb f8efd3 e0d2b8 f9f4e6 ffffff
  //   f9f4db 6a615b 4 0 32303c 737477 848888 b0b19 9 9 3 8*ffffff 4*2 0 0 979793 ffffff ffffff ffffff
  //   fefef4 f7f7e8 fafbf3 ffffff f3f2ec f9f9f1 fffff9 fffff7 fffffb ffffff 727277 5261 19bbc3 7b3bf
  //   11c9d8 17afc1 849b 186876 b89d87 ffffeb ffffeb fff0d1 fff3d4 fff4dc fff6de fff6db fff5da fff5d9
  //   fff4d9 fff3d6 fff8db ffffea ffffff fffff5 83796b 3000d 70919 707577 babeb9 ccd2c9 ffffff b6baba 0 2
  //   0 0 8*ffffff 5 6 6 6 0 5b5a59 ffffff f5f5eb f5f1e6 f7f5eb faf9eb fffffc fffffd b5b4b2 908d91 ecebe5
  //   ffffff fffff7 fffff6 ffffff fef4ef 74969c b788d a4be 10ebff 13d5eb 16b1c4 19d0e0 a1b8 658a88 ffe7c8
  //   ffffed fff4dd fff5dd fff3d7 fff2d4 fff1d6 fff3d6 fff3d7 fff1d5 fffde4 ffffff b9b09e 100c17 1a1d2b
  //   939a99 fdfff4 fffffc f1fcee e9ede7 cacfcc 90b12 4*0 8*ffffff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
endmodule

module PLU_COLOR_ALU (
  input  [7:0] DATA_A,
  input  EN_A,
  input  EN_OUT,
  input  [7:0] DATA_B,
  input  EN_B,
  input  CLK,
  input  [5:0] opcode,
  output [7:0] DOUT,
  output pixel_clk
);

  wire alu_1_opcode_out;
  wire [7:0] alu_1_dout, demultiplexer_1_out0, demultiplexer_1_out1, multiplexer_1_out, register_1_q,
       register_2_q, register_3_q;

  // Probe on opcode
  Multiplexer #(.width(8)) multiplexer_1 (
    .in0(demultiplexer_1_out0), .in1(DATA_A), .out(multiplexer_1_out), .sel(alu_1_opcode_out));
  // Probe on opcode[4:0]
  // Probe on multiplexer_1_out
  Register register_1 (.D(multiplexer_1_out), .en(EN_A), .clk(CLK), .Q(register_1_q), .clr(1'b0));
  Register register_2 (.D(DATA_B), .en(EN_B), .clk(CLK), .Q(register_2_q), .clr(1'b0));
  // Probe on register_2_q
  // Probe on register_1_q
  // Probe on demultiplexer_1_out0
  ALU alu_1 (
    .A(register_1_q), .B(register_2_q), .opcode(opcode[4:0]), .DOUT(alu_1_dout), .opcode_out(alu_1_opcode_out));
  // Probe on alu_1_dout
  Register register_3 (.D(alu_1_dout), .en(EN_OUT), .clk(CLK), .Q(register_3_q), .clr(1'b0));
  // Probe on register_3_q
  Demultiplexer #(.width(8)) demultiplexer_1 (
    .out0(demultiplexer_1_out0), .out1(demultiplexer_1_out1), .in(register_3_q), .sel(opcode[5]));
  // Probe on demultiplexer_1_out1
  Register register_4 (.D(demultiplexer_1_out1), .en(opcode[5]), .clk(CLK), .Q(DOUT), .clr(1'b0));

  assign pixel_clk = opcode[5];
endmodule

module PLU (
  input  [23:0] DATA_A_IN_24,
  input  [23:0] DATA_B_IN_24,
  input  [2:0] EN_A_3,
  input  [2:0] EN_B_3,
  input  [5:0] Channel_Swap_6,
  input  CLK,
  input  [17:0] opcode_in_18,
  output [23:0] RGB_OUTPUT_24,
  output pixel_clk
);

  wire plu_color_alu_1_pixel_clk, plu_color_alu_2_pixel_clk, plu_color_alu_3_pixel_clk;
  wire [7:0] plu_color_alu_1_dout, plu_color_alu_2_dout, plu_color_alu_3_dout;

  // Probe on opcode_in_18
  // Probe on opcode_in_18[17:12]
  // Probe on opcode_in_18[11:6]
  // Probe on opcode_in_18[5:0]
  PLU_COLOR_ALU plu_color_alu_1 (
    .DATA_A(DATA_A_IN_24[23:16]), .EN_A(EN_A_3[2]), .EN_OUT(1'b1), .DATA_B(DATA_B_IN_24[23:16]),
    .EN_B(EN_B_3[2]), .CLK(CLK), .opcode(opcode_in_18[17:12]), .DOUT(plu_color_alu_1_dout),
    .pixel_clk(plu_color_alu_1_pixel_clk));
  PLU_COLOR_ALU plu_color_alu_2 (
    .DATA_A(DATA_A_IN_24[15:8]), .EN_A(EN_A_3[1]), .EN_OUT(1'b1), .DATA_B(DATA_B_IN_24[15:8]),
    .EN_B(EN_B_3[1]), .CLK(CLK), .opcode(opcode_in_18[11:6]), .DOUT(plu_color_alu_2_dout),
    .pixel_clk(plu_color_alu_2_pixel_clk));
  PLU_COLOR_ALU plu_color_alu_3 (
    .DATA_A(DATA_A_IN_24[7:0]), .EN_A(EN_A_3[0]), .EN_OUT(1'b1), .DATA_B(DATA_B_IN_24[7:0]),
    .EN_B(EN_B_3[0]), .CLK(CLK), .opcode(opcode_in_18[5:0]), .DOUT(plu_color_alu_3_dout),
    .pixel_clk(plu_color_alu_3_pixel_clk));
  // Probe on plu_color_alu_1_dout
  // Probe on plu_color_alu_2_dout
  // Probe on plu_color_alu_3_dout
  COLOR_MUX color_mux_1 (
    .RED_IN(plu_color_alu_1_dout), .GREEN_IN(plu_color_alu_2_dout), .BLUE_IN(plu_color_alu_3_dout),
    .RGB_SELECT(Channel_Swap_6), .RGB_OUT(RGB_OUTPUT_24));
  or or_1 (pixel_clk, plu_color_alu_1_pixel_clk, plu_color_alu_2_pixel_clk, plu_color_alu_3_pixel_clk);
endmodule

module COLOR_MUX (
  input  [7:0] RED_IN,
  input  [7:0] GREEN_IN,
  input  [7:0] BLUE_IN,
  input  [5:0] RGB_SELECT,
  output [23:0] RGB_OUT
);

  Multiplexer #(.select(2), .width(8)) multiplexer_1 (
    .in0(RED_IN), .in1(GREEN_IN), .in2(BLUE_IN), .in3({8{1'b0}}), .out(RGB_OUT[23:16]), .sel(RGB_SELECT[5:4]));
  Multiplexer #(.select(2), .width(8)) multiplexer_2 (
    .in0(RED_IN), .in1(GREEN_IN), .in2(BLUE_IN), .in3({8{1'b0}}), .out(RGB_OUT[15:8]), .sel(RGB_SELECT[3:2]));
  Multiplexer #(.select(2), .width(8)) multiplexer_3 (
    .in0(RED_IN), .in1(GREEN_IN), .in2(BLUE_IN), .in3({8{1'b0}}), .out(RGB_OUT[7:0]), .sel(RGB_SELECT[1:0]));
  // Probe on RGB_SELECT[5:4]
  // Probe on RGB_SELECT[3:2]
  // Probe on RGB_SELECT[1:0]
endmodule

module ALU (
  input  [7:0] A,
  input  [7:0] B,
  input  [4:0] opcode,
  output [7:0] DOUT,
  output opcode_out
);

  wire [7:0] adder_1_out, and_1_out, divider_1_out, multiplier_1_out, nand_1_out, nor_1_out, not_1_out,
       or_1_out, shifter_1_out, subtractor_1_out, xnor_1_out, xor_1_out;

  Adder adder_1 (.a(A), .b(B), .out(adder_1_out));  // open: cin, cout
  Subtractor subtractor_1 (.a(A), .b(B), .out(subtractor_1_out));  // open: bin, bout
  Multiplier multiplier_1 (.a(A), .b(B), .out(multiplier_1_out));  // open: cin, cout
  Divider divider_1 (.a(A), .b(B), .out(divider_1_out));  // open: upper, rem
  Shifter shifter_1 (.in(A), .\dist (B[2:0]), .out(shifter_1_out));
  assign not_1_out = ~A;  // NOT_Gate not_1, 8 bits wide
  assign and_1_out = A & B;  // AND_Gate and_1, 8 bits wide
  assign or_1_out = A | B;  // OR_Gate or_1, 8 bits wide
  assign nand_1_out = ~(A & B);  // NAND_Gate nand_1, 8 bits wide
  assign nor_1_out = ~(A | B);  // NOR_Gate nor_1, 8 bits wide
  assign xor_1_out = A ^ B;  // XOR_Gate xor_1, 8 bits wide
  assign xnor_1_out = ~(A ^ B);  // XNOR_Gate xnor_1, 8 bits wide
  Multiplexer #(.select(4), .width(8)) multiplexer_1 (
    .in0(A), .in1(B), .in2(adder_1_out), .in3(subtractor_1_out), .in4(multiplier_1_out), .in5(divider_1_out),
    .in6(shifter_1_out), .in7(not_1_out), .in8(and_1_out), .in9(or_1_out), .in10(nand_1_out),
    .in11(nor_1_out), .in12(xor_1_out), .in13(xnor_1_out), .in14({8{1'b0}}), .in15({8{1'b1}}), .out(DOUT),
    .sel(opcode[3:0]));

  assign opcode_out = opcode[4];
endmodule
