// Logisim project RGB_TO_HSV_INT.circ as structural Verilog: 10 circuits, main circuit main
module main (
);

  wire [7:0] rgb2hsv_1_v;
  wire [15:0] rgb2hsv_1_s;
  wire [23:0] rgb2hsv_1_h;

  // Probe on 8'h19
  // Probe on 8'ha7
  // Probe on 8'he8
  RGB2HSV rgb2hsv_1 (.R_IN(8'h19), .B_IN(8'ha7), .G_IN(8'he8), .H(rgb2hsv_1_h), .S(rgb2hsv_1_s), .V(rgb2hsv_1_v));
  // Probe on rgb2hsv_1_h
  // Probe on rgb2hsv_1_s
  // Probe on rgb2hsv_1_v
endmodule

module RGB2HSV (
  input  [7:0] R_IN,
  input  [7:0] B_IN,
  input  [7:0] G_IN,
  output [23:0] H,
  output [15:0] S,
  output [7:0] V
);

  wire [7:0] rgb_max_sel_1_diff, rgb_max_sel_1_idx, rgb_max_sel_1_max, rgb_max_sel_1_mid, rgb_max_sel_1_min;

  RGB_MAX_SEL rgb_max_sel_1 (
    .R_IN(R_IN), .G_IN(B_IN), .B_IN(G_IN), .MAX(rgb_max_sel_1_max), .IDX(rgb_max_sel_1_idx),
    .DIFF(rgb_max_sel_1_diff), .MID(rgb_max_sel_1_mid), .MIN(rgb_max_sel_1_min));
  H_CALC h_calc_1 (
    .MIN(rgb_max_sel_1_min), .IDX(rgb_max_sel_1_idx), .DIFF(rgb_max_sel_1_diff), .MID(rgb_max_sel_1_mid),
    .H(H));
  S_CALC s_calc_1 (.DIFF(rgb_max_sel_1_diff), .V(V), .S(S));
  V_CALC v_calc_1 (.MAX(rgb_max_sel_1_max), .V(V));
endmodule

module RGB_MAX_SEL (
  input  [7:0] R_IN,
  input  [7:0] G_IN,
  input  [7:0] B_IN,
  output [7:0] MAX,
  output [7:0] IDX,
  output [7:0] DIFF,
  output [7:0] MID,
  output [7:0] MIN
);

  wire comparator_1_eq, comparator_1_gt, comparator_1_lt, comparator_2_eq, comparator_2_gt, comparator_2_lt,
       comparator_3_eq, comparator_3_gt, comparator_3_lt, minmax_1_bmax, minmax_1_bmin, minmax_1_gmax,
       minmax_1_gmin, minmax_1_rmax, minmax_1_rmin, nor_1_out, or_1_out, or_2_out, or_3_out, or_4_out,
       or_5_out, or_6_out, rgbl_sel_1_bmin, rgbl_sel_1_gmin_1, rgbl_sel_1_gmin_2, rgbl_sel_1_rmin_1,
       rgbl_sel_1_rmin_2, rgbm_sel_1_bmax_1, rgbm_sel_1_bmax_2, rgbm_sel_1_gmax_1, rgbm_sel_1_gmax_2,
       rgbm_sel_1_rmax;
  wire [1:0] priority_encoder_1_out, priority_encoder_2_out;

  Comparator #(.mode("unsigned")) comparator_1 (
    .a(R_IN), .b(G_IN), .gt(comparator_1_gt), .eq(comparator_1_eq), .lt(comparator_1_lt));
  Comparator #(.mode("unsigned")) comparator_2 (
    .a(R_IN), .b(B_IN), .gt(comparator_2_gt), .eq(comparator_2_eq), .lt(comparator_2_lt));
  Comparator #(.mode("unsigned")) comparator_3 (
    .a(G_IN), .b(B_IN), .gt(comparator_3_gt), .eq(comparator_3_eq), .lt(comparator_3_lt));
  nor nor_1 (nor_1_out, comparator_1_eq, comparator_2_eq, comparator_3_eq);
  RGBM_SEL rgbm_sel_1 (
    .RG_G(comparator_1_gt), .GB_E(comparator_3_eq), .RG_L(comparator_1_lt), .RB_E(comparator_2_eq),
    .RB_G(comparator_2_gt), .RG_E(comparator_1_eq), .RB_L(comparator_2_lt), .RMAX(rgbm_sel_1_rmax),
    .GMAX_1(rgbm_sel_1_gmax_1), .GMAX_2(rgbm_sel_1_gmax_2), .BMAX_1(rgbm_sel_1_bmax_1),
    .BMAX_2(rgbm_sel_1_bmax_2));
  MinMax minmax_1 (
    .RG_G(comparator_1_gt), .RG_L(comparator_1_lt), .RB_G(comparator_2_gt), .RB_L(comparator_2_lt),
    .GB_G(comparator_3_gt), .GB_L(comparator_3_lt), .EN(nor_1_out), .RMAX(minmax_1_rmax),
    .GMAX(minmax_1_gmax), .BMAX(minmax_1_bmax), .RMIN(minmax_1_rmin), .GMIN(minmax_1_gmin),
    .BMIN(minmax_1_bmin));
  RGBL_SEL rgbl_sel_1 (
    .RG_G(comparator_1_gt), .GB_E(comparator_3_eq), .RG_L(comparator_1_lt), .RB_E(comparator_2_eq),
    .RB_L(comparator_2_lt), .RG_E(comparator_1_eq), .RB_G(comparator_2_gt), .RMIN_1(rgbl_sel_1_rmin_1),
    .RMIN_2(rgbl_sel_1_rmin_2), .GMIN_1(rgbl_sel_1_gmin_1), .GMIN_2(rgbl_sel_1_gmin_2), .BMIN(rgbl_sel_1_bmin));
  or or_1 (or_1_out, minmax_1_rmax, rgbm_sel_1_rmax);
  or or_2 (or_2_out, minmax_1_bmin, rgbl_sel_1_bmin);
  or or_3 (or_3_out, minmax_1_gmax, rgbm_sel_1_gmax_1, rgbm_sel_1_gmax_2);
  or or_4 (or_4_out, minmax_1_bmax, rgbm_sel_1_bmax_1, rgbm_sel_1_bmax_2);
  or or_5 (or_5_out, minmax_1_gmin, rgbl_sel_1_gmin_2, rgbl_sel_1_gmin_1);
  or or_6 (or_6_out, minmax_1_rmin, rgbl_sel_1_rmin_2, rgbl_sel_1_rmin_1);
  RGB_SEL rgb_sel_1 (
    .R_IN(R_IN), .G_IN(G_IN), .B_IN(B_IN), .R_EN(or_1_out), .G_EN(or_3_out), .B_EN(or_4_out), .RGB_OUT(MAX));
  // Probe on priority_encoder_1_out
  Priority_Encoder #(.select(2)) priority_encoder_1 (
    .in0(or_1_out), .in1(or_3_out), .in2(or_4_out), .out(priority_encoder_1_out));  // open: in3, gs, en_out, en_in
  // Probe on priority_encoder_2_out
  Priority_Encoder #(.select(2)) priority_encoder_2 (
    .in0(or_6_out), .in1(or_5_out), .in2(or_2_out), .out(priority_encoder_2_out));  // open: in3, gs, en_out, en_in
  RGB_SEL rgb_sel_2 (
    .R_IN(R_IN), .G_IN(G_IN), .B_IN(B_IN), .R_EN(or_6_out), .G_EN(or_5_out), .B_EN(or_2_out), .RGB_OUT(MIN));
  Subtractor subtractor_1 (.a(MAX), .b(MIN), .out(DIFF));  // open: bin, bout
  // Probe on MAX
  Multiplexer #(.select(4), .width(8)) multiplexer_1 (
    .in0({8{1'b1}}), .in1(8'h2), .in2(8'h3), .in3({8{1'b1}}), .in4(8'h5), .in5({8{1'b1}}), .in6(8'h4),
    .in7({8{1'b1}}), .in8({8{1'b0}}), .in9(8'h1), .in10({8{1'b1}}), .in11({8{1'b1}}), .in12({8{1'b1}}),
    .in13({8{1'b1}}), .in14({8{1'b1}}), .in15({8{1'b1}}), .out(IDX),
    .sel({priority_encoder_2_out, priority_encoder_1_out}));
  Divider divider_1 (.a(DIFF), .b(8'h2), .out(MID));  // open: upper, rem
  // Probe on MIN

  // Notes on the sheet:
  //   RG
  //   RB
  //   GB
endmodule

module H_CALC (
  input  [7:0] MIN,
  input  [7:0] IDX,
  input  [7:0] DIFF,
  input  [7:0] MID,
  output [23:0] H
);

  wire bit_extender_3_out;
  wire [7:0] subtractor_1_out, xor_1_out;
  wire [23:0] adder_1_out, bit_extender_1_out, bit_extender_2_out, bit_extender_4_out, divider_1_out,
       multiplexer_1_out, multiplier_1_out, shifter_1_out, subtractor_2_out;

  // Probe on MIN
  // Probe on DIFF
  // Probe on MID
  // Probe on subtractor_1_out
  Subtractor subtractor_1 (.a(MID), .b(MIN), .out(subtractor_1_out));  // open: bin, bout
  // Probe on bit_extender_1_out
  assign bit_extender_1_out = {{16{1'b0}}, subtractor_1_out};  // Bit_Extender bit_extender_1
  assign bit_extender_2_out = {{16{1'b0}}, DIFF};  // Bit_Extender bit_extender_2
  assign xor_1_out = IDX ^ {8{1'b0}};  // XOR_Gate xor_1, 8 bits wide
  // Probe on shifter_1_out
  Shifter #(.width(24)) shifter_1 (.in(bit_extender_1_out), .\dist (5'b10000), .out(shifter_1_out));
  // Probe on xor_1_out
  Bit_Extender #(.out_width(1), .\type ("input")) bit_extender_3 (
    .in(xor_1_out), .out(bit_extender_3_out));  // open: extend
  // Probe on divider_1_out
  Divider #(.width(24)) divider_1 (.a(shifter_1_out), .b(bit_extender_2_out), .out(divider_1_out));  // open: upper, rem
  // Probe on adder_1_out
  Adder #(.width(24)) adder_1 (.a(divider_1_out), .b(24'h1), .out(adder_1_out));  // open: cin, cout
  Subtractor #(.width(24)) subtractor_2 (.a(24'hffff), .b(adder_1_out), .out(subtractor_2_out));  // open: bin, bout
  Multiplexer #(.width(24)) multiplexer_1 (
    .in0(adder_1_out), .in1(subtractor_2_out), .out(multiplexer_1_out), .sel(bit_extender_3_out));
  // Probe on 24'hffff
  assign bit_extender_4_out = {{16{1'b0}}, IDX};  // Bit_Extender bit_extender_4
  // Probe on IDX
  Multiplier #(.width(24)) multiplier_1 (
    .a(24'hffff), .b(bit_extender_4_out), .out(multiplier_1_out));  // open: cin, cout
  Adder #(.width(24)) adder_2 (.a(multiplexer_1_out), .b(multiplier_1_out), .out(H));  // open: cin, cout
  // Probe on multiplier_1_out
  // Probe on H

  // Notes on the sheet:
  //   F
endmodule

module S_CALC (
  input  [7:0] DIFF,
  input  [7:0] V,
  output [15:0] S
);

  wire [23:0] bit_extender_1_out, bit_extender_2_out, divider_1_out, shifter_1_out, subtractor_1_out;

  // Probe on DIFF
  assign bit_extender_1_out = {{16{1'b0}}, DIFF};  // Bit_Extender bit_extender_1
  // Probe on V
  assign bit_extender_2_out = {{16{1'b0}}, V};  // Bit_Extender bit_extender_2
  // Probe on bit_extender_1_out
  // Probe on shifter_1_out
  // Probe on shifter_1_out
  Shifter #(.width(24)) shifter_1 (.in(bit_extender_1_out), .\dist (5'b10000), .out(shifter_1_out));
  // Probe on bit_extender_2_out
  Subtractor #(.width(24)) subtractor_1 (.a(shifter_1_out), .b(24'h1), .out(subtractor_1_out));  // open: bin, bout
  // Probe on divider_1_out
  Bit_Extender #(.in_width(24), .\type ("zero")) bit_extender_3 (.in(divider_1_out), .out(S));
  Divider #(.width(24)) divider_1 (
    .a(subtractor_1_out), .b(bit_extender_2_out), .out(divider_1_out));  // open: upper, rem
endmodule

module V_CALC (
  input  [7:0] MAX,
  output [7:0] V
);


  assign V = MAX;
endmodule

module MinMax (
  input  RG_G,
  input  RG_L,
  input  RB_G,
  input  RB_L,
  input  GB_G,
  input  GB_L,
  input  EN,
  output RMAX,
  output GMAX,
  output BMAX,
  output RMIN,
  output GMIN,
  output BMIN
);

  wire and_1_out, and_2_out, and_3_out, and_4_out, and_5_out, and_6_out;

  and and_1 (and_1_out, RG_G, RB_G);
  and and_2 (and_2_out, RG_L, GB_G);
  and and_3 (and_3_out, RB_L, GB_L);
  and and_4 (and_4_out, RG_L, RB_L);
  and and_5 (and_5_out, RG_G, GB_L);
  and and_6 (and_6_out, RB_G, GB_G);
  and and_7 (RMAX, and_1_out, EN);
  and and_8 (GMAX, and_2_out, EN);
  and and_9 (BMAX, and_3_out, EN);
  and and_10 (RMIN, and_4_out, EN);
  and and_11 (GMIN, and_5_out, EN);
  and and_12 (BMIN, and_6_out, EN);

  // Notes on the sheet:
  //   R max
  //   G max
  //   B max
  //   R min
  //   G min
  //   B min
endmodule

module RGB_SEL (
  input  [7:0] R_IN,
  input  [7:0] G_IN,
  input  [7:0] B_IN,
  input  R_EN,
  input  G_EN,
  input  B_EN,
  output [7:0] RGB_OUT
);

  wire [1:0] priority_encoder_1_out;
  wire [7:0] and_1_out, and_2_out, and_3_out, bit_extender_1_out, bit_extender_2_out, bit_extender_3_out;

  assign bit_extender_1_out = {{7{1'b1}}, R_EN};  // Bit_Extender bit_extender_1
  assign bit_extender_2_out = {{7{1'b1}}, G_EN};  // Bit_Extender bit_extender_2
  assign bit_extender_3_out = {{7{1'b1}}, B_EN};  // Bit_Extender bit_extender_3
  assign and_1_out = bit_extender_1_out & R_IN;  // AND_Gate and_1, 8 bits wide
  assign and_2_out = bit_extender_2_out & G_IN;  // AND_Gate and_2, 8 bits wide
  assign and_3_out = bit_extender_3_out & B_IN;  // AND_Gate and_3, 8 bits wide
  // Probe on and_1_out
  Priority_Encoder #(.select(2)) priority_encoder_1 (
    .in0(R_EN), .in1(G_EN), .in2(B_EN), .in3(1'b0), .out(priority_encoder_1_out));  // open: gs, en_out, en_in
  // Probe on RGB_OUT
  Multiplexer #(.select(2), .width(8)) multiplexer_1 (
    .in0(and_1_out), .in1(and_2_out), .in2(and_3_out), .in3({8{1'b0}}), .out(RGB_OUT),
    .sel(priority_encoder_1_out));
endmodule

module RGBM_SEL (
  input  RG_G,
  input  GB_E,
  input  RG_L,
  input  RB_E,
  input  RB_G,
  input  RG_E,
  input  RB_L,
  output RMAX,
  output GMAX_1,
  output GMAX_2,
  output BMAX_1,
  output BMAX_2
);

  wire and_1_out, and_2_out, and_3_out, and_5_out;

  and and_1 (and_1_out, GB_E, RB_E, RG_E);
  and and_2 (and_2_out, RG_G, GB_E);
  and and_3 (and_3_out, GB_E, RG_L);
  and and_4 (BMAX_1, RG_G, RB_E);
  and and_5 (and_5_out, RB_E, RG_L);
  and and_6 (GMAX_2, RB_G, RG_E);
  and and_7 (BMAX_2, RG_E, RB_L);
  or or_1 (RMAX, and_1_out, and_2_out);
  or or_2 (GMAX_1, and_3_out, and_5_out);
endmodule

module RGBL_SEL (
  input  RG_G,
  input  GB_E,
  input  RG_L,
  input  RB_E,
  input  RB_L,
  input  RG_E,
  input  RB_G,
  output RMIN_1,
  output RMIN_2,
  output GMIN_1,
  output GMIN_2,
  output BMIN
);

  wire and_2_out, and_4_out, and_6_out, and_7_out;

  and and_1 (GMIN_1, RG_G, GB_E);
  and and_2 (and_2_out, GB_E, RG_L);
  and and_3 (GMIN_2, RG_G, RB_E);
  and and_4 (and_4_out, RB_E, RG_L);
  and and_5 (RMIN_1, RB_L, RG_E);
  and and_6 (and_6_out, RG_E, RB_G);
  and and_7 (and_7_out, RG_E, RB_E, GB_E);
  or or_1 (BMIN, and_6_out, and_7_out);
  or or_2 (RMIN_2, and_2_out, and_4_out);
endmodule
